# Fritzing sketch SensorAssignment (saved by Fritzing 0.9.3b)
breadboards: 1

parts:
  Part1 = Arduino Uno (Rev3)
  RHT1 = Humidity and Temperature Sensor RHT03
  R1 = Resistor [tolerance=±5% resistance=10k package="0805 [SMD]"]
  R2 = PHOTOCELL [package=photocell]
  R3 = Resistor [tolerance=±5% resistance=10k package="0805 [SMD]"]
  Part2 = MicroSD Card Module
  U1 = DS1307 [package=so08]

nets:
  N1: Part1.A4/SDA, U1.SQW
  N2: Part1.A5/SCL, U1.SCL
  N3: Part1.D10_PWM/SS, Part2.CS
  N4: Part1.D11_PWM/MOSI, Part2.MOSI
  N5: Part1.D12/MISO, Part2.MISO
  N6: Part1.D13/SCK, Part2.SCK
  N7: Part1.GND, RHT1.GND_1
  VCC: RHT1.Vcc, R1.Pin_0, Part2.VCC, U1.VCC
  N8: RHT1.Data-signal, R1.Pin_1
  N9: R2.P$1, R3.Pin_0, R3.Pin_1
